# Fritzing sketch 小车 (saved by Fritzing 0.9.10b)
breadboards: 1

parts:
  M1 = STM32F103C8T6 blue mini board
  HC-SR04_Sensor_1 = HC-SR04 Ultrasonic Distance Sensor
  M2 = gear-motor
  A2 = ky-033 [package=THT]
  A3 = ky-033 [package=THT]
  A4 = ky-033 [package=THT]
  A5 = ky-033 [package=THT]
  M3 = gear-motor
  M4 = gear-motor
  M5 = gear-motor
  J1 = Basic Servo
  YwRobot_Power_Supply1 = YwRobot Breadboard Power Supply [part_number=545043]
  元件4 = Motor Driver 1A Dual TB6612FNG
  BT1 = Bluetooth HC-06u [package=THT]
  A6 = STLINK

nets:
  N1: M1.B12, HC-SR04_Sensor_1.TRIG
  N2: M1.B13, HC-SR04_Sensor_1.ECHO
  N3: M1.B15, A4.pin2
  N4: M1.A9, BT1.RXD
  N5: M1.A10, BT1.TXD
  N6: M1.B6, A5.pin2
  N7: M1.B7, A3.pin2
  N8: M1.B8, A2.pin2
  GND: M1.G, M1.GND, HC-SR04_Sensor_1.GND, A2.pin3, A3.pin3, A4.pin3, A5.pin3, YwRobot_Power_Supply1.GND#13, YwRobot_Power_Supply1.GND#14, BT1.GND, A6.Pin_3, A6.Pin_4
  VCC: M1.3.3V, M1.3.3, HC-SR04_Sensor_1.VCC, A2.pin4, A3.pin4, A4.pin4, A5.pin4, YwRobot_Power_Supply1.VCC#9, YwRobot_Power_Supply1.VCC#10, 元件4.VCC, 元件4.STBY, A6.Pin_7, A6.Pin_8
  N9: M1.A5, 元件4.AIN2
  N10: M1.A6, 元件4.BIN1
  N11: M1.A7, 元件4.BIN2
  N12: M1.B0, J1.pulse
  N13: M1.DIO, A6.Pin_2
  N14: M1.CLK, A6.Pin_6
  N15: M2.pin_1, M3.pin_2, 元件4.B01
  N16: M2.pin_2, M3.pin_1, 元件4.B02
  N17: M4.pin_1, M5.pin_2, 元件4.A01
  N18: M4.pin_2, M5.pin_1, 元件4.A02
  GND_2: J1.gnd, YwRobot_Power_Supply1.GND#11, YwRobot_Power_Supply1.GND#12, 元件4.GND
  VCC_2: J1.vcc, YwRobot_Power_Supply1.VCC#5, YwRobot_Power_Supply1.VCC#6, 元件4.VM, BT1.VCC

notes:
  左轮 后-前
  电机（上线-下线）
  右轮 后-前
  电机（上线-下线）

custom parts:
  ky-033: KY-033 Line successor module with TCRT5000 and analog output.
  YwRobot Breadboard Power Supply: The YwRobot Breadboard Power Supply (MB-V2) has two power rails; they can be 5V or 3V3. Power to the module can be provided through the female USB socket or through the A10 (female) 2.1mm power jack.
  Bluetooth HC-06u: Bluetooth HC-06 - face up, pins down 16.5mm x 37.5mm PCB
  STLINK: STLINK.
